// Digital circuit BW8cpu.dig as structural Verilog
module BW8cpu (
);

  wire a_dbus_a, a_dbus_l, a_lhs_a, a_rhs_a, addr_a, addr_bus, b_dbus_a, b_dbus_l, b_lhs_a, b_rhs_a,
       c_dbus_a, c_dbus_l, c_lhs_a, c_rhs_a, clr, d_dbus_a, d_dbus_l, d_lhs_a, d_rhs_a, dbus_a, dbus_l,
       ir_dbus_l, mem_dbus_a, mem_dbus_l, xfer, xfer_a, xfer_l;
  wire [7:0] clk, dbus, lhs, mbus, rhs;

  control_unit Control_Unit ();  // open: nirq, clk, opcode, flags, nrst, nreq, dbus_assert, dbus_load, alu_op, xfer_assert, xfer_load, addr_assert, count, dec_sp, nbrk, nclk
  // instruction_register Instruction_Register: pin names not known; wires that end beside it: clk, dbus, ir_dbus_l, clr
  memory_bridge Memory_Bridge (.dbus_assert(mem_dbus_a), .dbus_load(mem_dbus_l), .dbus(dbus), .mbus(mbus));
  // accumulator Accumulator: pin names not known; wires that end beside it: a_dbus_l, b_dbus_l, a_dbus_a, b_dbus_a, a_lhs_a, b_lhs_a, a_rhs_a, b_rhs_a, dbus, xfer, clk, clr, addr_bus
  general_purpose_register C_Register (
    .DBUS_IN(clk), .CLK(c_dbus_l), .DBUS_LOAD(c_dbus_a), .DBUS_ASSERT(c_lhs_a), .LHS_ASSERT(c_rhs_a),
    .RHS_ASSERT(clr), .CLR(dbus[0]), .LHS(lhs), .RHS(rhs));  // open: DBUS_OUT
  general_purpose_register D_Register (
    .DBUS_IN(clk), .CLK(d_dbus_l), .DBUS_LOAD(d_dbus_a), .DBUS_ASSERT(d_lhs_a), .LHS_ASSERT(d_rhs_a),
    .RHS_ASSERT(clr), .CLR(dbus[0]), .LHS(lhs), .RHS(rhs));  // open: DBUS_OUT
  // bus_controller Bus_Controller: pin names not known; wires that end beside it: dbus_a, dbus_l, xfer_a, xfer_l, addr_a, a_dbus_a, b_dbus_a, c_dbus_a, d_dbus_a, mem_dbus_l, a_dbus_l, b_dbus_l, c_dbus_l, d_dbus_l, mem_dbus_a
  address_register Program_Counter ();  // open: xfer, clk, clr, xfer_load, addr_assert, xfer_assert, inc, dec, addr
  address_register Stack_Pointer ();  // open: xfer, clk, clr, xfer_load, addr_assert, xfer_assert, inc, dec, addr
  address_register X_Index ();  // open: xfer, clk, clr, xfer_load, addr_assert, xfer_assert, inc, dec, addr
  address_register Y_Index ();  // open: xfer, clk, clr, xfer_load, addr_assert, xfer_assert, inc, dec, addr
  // Pins of 1 and 8 bits meet at dbus
endmodule
